// Logisim project 24,PRACTICLE1.circ as structural Verilog
module Q2_A (
);

  // NAND_Gate nand_1 is placed but not wired
  // NAND_Gate nand_2 is placed but not wired
endmodule

module Q4 (
  input  A,
  input  B,
  input  C,
  output D
);

  wire nand_1_out, not_1_out;

  nand nand_1 (nand_1_out, A, B);
  not not_1 (not_1_out, C);
  nor nor_1 (D, nand_1_out, not_1_out);
endmodule

module Q4_2 (
  input  A,
  input  B,
  input  C,
  output D
);

  wire and_1_out, nor_1_out;

  nor nor_1 (nor_1_out, A, B);
  and and_1 (and_1_out, B, C);
  or or_1 (D, nor_1_out, and_1_out);

  // Notes on the sheet:
  //   (A+B)
endmodule

module Q5_1 (
  input  in_1,
  input  in_2,
  output out_3
);

  and and_1 (out_3, in_1, in_1, in_2);
endmodule

module Q5_2 (
  input  A,
  input  B,
  output C
);

  or or_1 (C, A, B);
endmodule

module Q6 (
  input  A,
  input  B,
  input  C,
  output D
);

  wire not_1_out, or_1_out;

  not not_1 (not_1_out, C);
  or or_1 (or_1_out, A, B);
  and and_1 (D, or_1_out, not_1_out);
endmodule

module Q7 (
  input  in_1,
  input  in_2,
  input  in_3,
  input  in_4,
  input  in_5,
  input  in_6,
  output out_7,
  output out_8
);

  and and_1 (out_7, in_1, in_1, in_2, in_3);
  or or_1 (out_8, in_4, in_5, in_6);
endmodule

module Q8 (
  input  A,
  input  B,
  input  C,
  output out_4
);

  wire and_1_out;

  and and_1 (and_1_out, A, B);
  or or_1 (out_4, and_1_out, C);

  // Notes on the sheet:
  //   A.B
  //   A.B+C
endmodule

module Q8_B (
  input  A,
  input  B,
  input  C,
  input  D,
  input  E,
  input  F,
  output G
);

  wire and_1_out, nand_1_out, nand_2_out;

  nand nand_1 (nand_1_out, A, A, B);
  and and_1 (and_1_out, C, C, D);
  nand nand_2 (nand_2_out, E, F);
  or or_1 (G, nand_1_out, and_1_out, nand_2_out);
endmodule

module Q8_C (
  input  in_1,
  output out_2
);

  wire not_1_out, or_1_out, or_2_out, or_3_out, undriven;

  not not_1 (not_1_out, in_1);
  or or_1 (or_1_out, not_1_out, in_1);
  or or_2 (or_2_out, in_1, undriven);
  buf or_3 (or_3_out, undriven);  // OR_Gate
  and and_1 (out_2, or_1_out, or_2_out, or_3_out);
endmodule
